# Fritzing sketch ESP01_Upload (saved by Fritzing 0.9.3b)
circuit board: 8.46667cm x 5.64444cm
breadboards: 1

parts:
  Espessif_Serial_Wifi_Modul_1 = ESP8266 ESP01 [part_number=ESP8266 package=THT]
  Composant1 = Arduino Uno (Rev3)
  R1 = Resistor [tolerance=±5% resistance=220 package=THT]  # not connected

nets (from the schematic view):
  GND: Espessif_Serial_Wifi_Modul_1.GND, Espessif_Serial_Wifi_Modul_1.GPIO00, Composant1.GND
  N1: Espessif_Serial_Wifi_Modul_1.RXD, Composant1.D0/RX
  N2: Espessif_Serial_Wifi_Modul_1.TXD, Composant1.D1/TX
  VCC: Espessif_Serial_Wifi_Modul_1.VCC, Espessif_Serial_Wifi_Modul_1.CH_PD, Composant1.3V3
  N3: Espessif_Serial_Wifi_Modul_1.GPIO16, Composant1.RESET

notes:
  Mettre GPIO0 à la masse active le mode programmation.
  Il faut RESET après un changement de mode.

custom parts:
  ESP8266 ESP01: Generic WiFi Module based on the ESP8266 with onboard PCB antenna and UART communications
